// Logisim project sqrt2.circ as structural Verilog: 26 circuits, main circuit main
module main (
  input  ENABLE,
  input  [15:0] IO_DATA_IN,
  output NAN,
  output PINF,
  output NINF,
  output RESULT,
  output [15:0] IO_DATA_OUT
);

  wire CLK_out;

  Clock CLK (.out(CLK_out));
  sqrt sqrt_1 (
    .CLK(CLK_out), .ENABLE(ENABLE), .IO_DATA_IN(IO_DATA_IN), .IS_NAN(NAN), .IS_PINF(PINF), .IS_NINF(NINF),
    .RESULT(RESULT), .IO_DATA_OUT(IO_DATA_OUT));
endmodule

module bit_summator (
  input  A,
  input  B,
  input  extra,
  output Sum,
  output res_extra
);

  wire and_1_out, and_2_out, xor_1_out;

  xor xor_1 (xor_1_out, A, B);
  and and_1 (and_1_out, A, B);
  and and_2 (and_2_out, xor_1_out, extra);
  xor xor_2 (Sum, xor_1_out, extra);
  or or_1 (res_extra, and_2_out, and_1_out);
endmodule

module summator (
  input  [23:0] B,
  input  [23:0] A,
  output [23:0] Sum
);

  wire bit_summator_1_res_extra, bit_summator_2_res_extra, bit_summator_3_res_extra,
       bit_summator_4_res_extra, bit_summator_5_res_extra, bit_summator_6_res_extra,
       bit_summator_7_res_extra, bit_summator_8_res_extra, bit_summator_9_res_extra,
       bit_summator_10_res_extra, bit_summator_11_res_extra, bit_summator_12_res_extra,
       bit_summator_13_res_extra, bit_summator_14_res_extra, bit_summator_15_res_extra,
       bit_summator_16_res_extra, bit_summator_17_res_extra, bit_summator_18_res_extra,
       bit_summator_19_res_extra, bit_summator_20_res_extra, bit_summator_21_res_extra,
       bit_summator_22_res_extra, bit_summator_23_res_extra;

  bit_summator bit_summator_1 (.A(A[0]), .B(B[0]), .extra(1'b0), .Sum(Sum[0]), .res_extra(bit_summator_1_res_extra));
  bit_summator bit_summator_2 (
    .A(A[1]), .B(B[1]), .extra(bit_summator_1_res_extra), .Sum(Sum[1]), .res_extra(bit_summator_2_res_extra));
  bit_summator bit_summator_3 (
    .A(A[2]), .B(B[2]), .extra(bit_summator_2_res_extra), .Sum(Sum[2]), .res_extra(bit_summator_3_res_extra));
  bit_summator bit_summator_4 (
    .A(A[3]), .B(B[3]), .extra(bit_summator_3_res_extra), .Sum(Sum[3]), .res_extra(bit_summator_4_res_extra));
  bit_summator bit_summator_5 (
    .A(A[4]), .B(B[4]), .extra(bit_summator_4_res_extra), .Sum(Sum[4]), .res_extra(bit_summator_5_res_extra));
  bit_summator bit_summator_6 (
    .A(A[5]), .B(B[5]), .extra(bit_summator_5_res_extra), .Sum(Sum[5]), .res_extra(bit_summator_6_res_extra));
  bit_summator bit_summator_7 (
    .A(A[6]), .B(B[6]), .extra(bit_summator_6_res_extra), .Sum(Sum[6]), .res_extra(bit_summator_7_res_extra));
  bit_summator bit_summator_8 (
    .A(A[7]), .B(B[7]), .extra(bit_summator_7_res_extra), .Sum(Sum[7]), .res_extra(bit_summator_8_res_extra));
  bit_summator bit_summator_9 (
    .A(A[8]), .B(B[8]), .extra(bit_summator_8_res_extra), .Sum(Sum[8]), .res_extra(bit_summator_9_res_extra));
  bit_summator bit_summator_10 (
    .A(A[9]), .B(B[9]), .extra(bit_summator_9_res_extra), .Sum(Sum[9]), .res_extra(bit_summator_10_res_extra));
  bit_summator bit_summator_11 (
    .A(A[10]), .B(B[10]), .extra(bit_summator_10_res_extra), .Sum(Sum[10]),
    .res_extra(bit_summator_11_res_extra));
  bit_summator bit_summator_12 (
    .A(A[11]), .B(B[11]), .extra(bit_summator_11_res_extra), .Sum(Sum[11]),
    .res_extra(bit_summator_12_res_extra));
  bit_summator bit_summator_13 (
    .A(A[12]), .B(B[12]), .extra(bit_summator_12_res_extra), .Sum(Sum[12]),
    .res_extra(bit_summator_13_res_extra));
  bit_summator bit_summator_14 (
    .A(A[13]), .B(B[13]), .extra(bit_summator_13_res_extra), .Sum(Sum[13]),
    .res_extra(bit_summator_14_res_extra));
  bit_summator bit_summator_15 (
    .A(A[14]), .B(B[14]), .extra(bit_summator_14_res_extra), .Sum(Sum[14]),
    .res_extra(bit_summator_15_res_extra));
  bit_summator bit_summator_16 (
    .A(A[15]), .B(B[15]), .extra(bit_summator_15_res_extra), .Sum(Sum[15]),
    .res_extra(bit_summator_16_res_extra));
  bit_summator bit_summator_17 (
    .A(A[16]), .B(B[16]), .extra(bit_summator_16_res_extra), .Sum(Sum[16]),
    .res_extra(bit_summator_17_res_extra));
  bit_summator bit_summator_18 (
    .A(A[17]), .B(B[17]), .extra(bit_summator_17_res_extra), .Sum(Sum[17]),
    .res_extra(bit_summator_18_res_extra));
  bit_summator bit_summator_19 (
    .A(A[18]), .B(B[18]), .extra(bit_summator_18_res_extra), .Sum(Sum[18]),
    .res_extra(bit_summator_19_res_extra));
  bit_summator bit_summator_20 (
    .A(A[19]), .B(B[19]), .extra(bit_summator_19_res_extra), .Sum(Sum[19]),
    .res_extra(bit_summator_20_res_extra));
  bit_summator bit_summator_21 (
    .A(A[20]), .B(B[20]), .extra(bit_summator_20_res_extra), .Sum(Sum[20]),
    .res_extra(bit_summator_21_res_extra));
  bit_summator bit_summator_22 (
    .A(A[21]), .B(B[21]), .extra(bit_summator_21_res_extra), .Sum(Sum[21]),
    .res_extra(bit_summator_22_res_extra));
  bit_summator bit_summator_23 (
    .A(A[22]), .B(B[22]), .extra(bit_summator_22_res_extra), .Sum(Sum[22]),
    .res_extra(bit_summator_23_res_extra));
  bit_summator bit_summator_24 (
    .A(A[23]), .B(B[23]), .extra(bit_summator_23_res_extra), .Sum(Sum[23]));  // open: res_extra
endmodule

module bit_substractor (
  input  A,
  input  B,
  input  Borrow_in,
  output Diff,
  output Borrow_out
);

  wire and_1_out, and_2_out, not_1_out, not_2_out, xor_1_out;

  not not_1 (not_1_out, A);
  xor xor_1 (xor_1_out, A, B);
  and and_1 (and_1_out, not_1_out, B);
  not not_2 (not_2_out, xor_1_out);
  xor xor_2 (Diff, xor_1_out, Borrow_in);
  and and_2 (and_2_out, Borrow_in, not_2_out);
  or or_1 (Borrow_out, and_2_out, and_1_out);
endmodule

module bit_shift_left (
  input  [23:0] in_1,
  output [23:0] out_2
);

  // NoConnect on in_1[23]

  assign out_2 = {in_1[22:0], 1'b0};
endmodule

module substractor (
  input  [23:0] B,
  input  [23:0] A,
  output [23:0] Res,
  output is_neg
);

  wire bit_substractor_1_borrow_out, bit_substractor_2_borrow_out, bit_substractor_3_borrow_out,
       bit_substractor_4_borrow_out, bit_substractor_5_borrow_out, bit_substractor_6_borrow_out,
       bit_substractor_7_borrow_out, bit_substractor_8_borrow_out, bit_substractor_9_borrow_out,
       bit_substractor_10_borrow_out, bit_substractor_11_borrow_out, bit_substractor_12_borrow_out,
       bit_substractor_13_borrow_out, bit_substractor_14_borrow_out, bit_substractor_15_borrow_out,
       bit_substractor_16_borrow_out, bit_substractor_17_borrow_out, bit_substractor_18_borrow_out,
       bit_substractor_19_borrow_out, bit_substractor_20_borrow_out, bit_substractor_21_borrow_out,
       bit_substractor_22_borrow_out, bit_substractor_23_borrow_out;

  bit_substractor bit_substractor_1 (
    .A(A[0]), .B(B[0]), .Borrow_in(1'b0), .Diff(Res[0]), .Borrow_out(bit_substractor_1_borrow_out));
  bit_substractor bit_substractor_2 (
    .A(A[1]), .B(B[1]), .Borrow_in(bit_substractor_1_borrow_out), .Diff(Res[1]),
    .Borrow_out(bit_substractor_2_borrow_out));
  bit_substractor bit_substractor_3 (
    .A(A[2]), .B(B[2]), .Borrow_in(bit_substractor_2_borrow_out), .Diff(Res[2]),
    .Borrow_out(bit_substractor_3_borrow_out));
  bit_substractor bit_substractor_4 (
    .A(A[3]), .B(B[3]), .Borrow_in(bit_substractor_3_borrow_out), .Diff(Res[3]),
    .Borrow_out(bit_substractor_4_borrow_out));
  bit_substractor bit_substractor_5 (
    .A(A[4]), .B(B[4]), .Borrow_in(bit_substractor_4_borrow_out), .Diff(Res[4]),
    .Borrow_out(bit_substractor_5_borrow_out));
  bit_substractor bit_substractor_6 (
    .A(A[5]), .B(B[5]), .Borrow_in(bit_substractor_5_borrow_out), .Diff(Res[5]),
    .Borrow_out(bit_substractor_6_borrow_out));
  bit_substractor bit_substractor_7 (
    .A(A[6]), .B(B[6]), .Borrow_in(bit_substractor_6_borrow_out), .Diff(Res[6]),
    .Borrow_out(bit_substractor_7_borrow_out));
  bit_substractor bit_substractor_8 (
    .A(A[7]), .B(B[7]), .Borrow_in(bit_substractor_7_borrow_out), .Diff(Res[7]),
    .Borrow_out(bit_substractor_8_borrow_out));
  bit_substractor bit_substractor_9 (
    .A(A[8]), .B(B[8]), .Borrow_in(bit_substractor_8_borrow_out), .Diff(Res[8]),
    .Borrow_out(bit_substractor_9_borrow_out));
  bit_substractor bit_substractor_10 (
    .A(A[9]), .B(B[9]), .Borrow_in(bit_substractor_9_borrow_out), .Diff(Res[9]),
    .Borrow_out(bit_substractor_10_borrow_out));
  bit_substractor bit_substractor_11 (
    .A(A[10]), .B(B[10]), .Borrow_in(bit_substractor_10_borrow_out), .Diff(Res[10]),
    .Borrow_out(bit_substractor_11_borrow_out));
  bit_substractor bit_substractor_12 (
    .A(A[11]), .B(B[11]), .Borrow_in(bit_substractor_11_borrow_out), .Diff(Res[11]),
    .Borrow_out(bit_substractor_12_borrow_out));
  bit_substractor bit_substractor_13 (
    .A(A[12]), .B(B[12]), .Borrow_in(bit_substractor_12_borrow_out), .Diff(Res[12]),
    .Borrow_out(bit_substractor_13_borrow_out));
  bit_substractor bit_substractor_14 (
    .A(A[13]), .B(B[13]), .Borrow_in(bit_substractor_13_borrow_out), .Diff(Res[13]),
    .Borrow_out(bit_substractor_14_borrow_out));
  bit_substractor bit_substractor_15 (
    .A(A[14]), .B(B[14]), .Borrow_in(bit_substractor_14_borrow_out), .Diff(Res[14]),
    .Borrow_out(bit_substractor_15_borrow_out));
  bit_substractor bit_substractor_16 (
    .A(A[15]), .B(B[15]), .Borrow_in(bit_substractor_15_borrow_out), .Diff(Res[15]),
    .Borrow_out(bit_substractor_16_borrow_out));
  bit_substractor bit_substractor_17 (
    .A(A[16]), .B(B[16]), .Borrow_in(bit_substractor_16_borrow_out), .Diff(Res[16]),
    .Borrow_out(bit_substractor_17_borrow_out));
  bit_substractor bit_substractor_18 (
    .A(A[17]), .B(B[17]), .Borrow_in(bit_substractor_17_borrow_out), .Diff(Res[17]),
    .Borrow_out(bit_substractor_18_borrow_out));
  bit_substractor bit_substractor_19 (
    .A(A[18]), .B(B[18]), .Borrow_in(bit_substractor_18_borrow_out), .Diff(Res[18]),
    .Borrow_out(bit_substractor_19_borrow_out));
  bit_substractor bit_substractor_20 (
    .A(A[19]), .B(B[19]), .Borrow_in(bit_substractor_19_borrow_out), .Diff(Res[19]),
    .Borrow_out(bit_substractor_20_borrow_out));
  bit_substractor bit_substractor_21 (
    .A(A[20]), .B(B[20]), .Borrow_in(bit_substractor_20_borrow_out), .Diff(Res[20]),
    .Borrow_out(bit_substractor_21_borrow_out));
  bit_substractor bit_substractor_22 (
    .A(A[21]), .B(B[21]), .Borrow_in(bit_substractor_21_borrow_out), .Diff(Res[21]),
    .Borrow_out(bit_substractor_22_borrow_out));
  bit_substractor bit_substractor_23 (
    .A(A[22]), .B(B[22]), .Borrow_in(bit_substractor_22_borrow_out), .Diff(Res[22]),
    .Borrow_out(bit_substractor_23_borrow_out));
  bit_substractor bit_substractor_24 (
    .A(A[23]), .B(B[23]), .Borrow_in(bit_substractor_23_borrow_out), .Diff(Res[23]), .Borrow_out(is_neg));
endmodule

module rs_trigger_sync (
  input  R,
  input  C,
  input  S,
  input  Enable,
  output Q,
  output NQ
);

  wire and_1_out, and_2_out, nor_2_out, not_1_out, or_1_out, por_1_out;

  not not_1 (not_1_out, Enable);
  and and_1 (and_1_out, R, C);
  and and_2 (and_2_out, C, S);
  POR por_1 (.out(por_1_out));
  or or_1 (or_1_out, not_1_out, por_1_out);
  nor nor_1 (Q, and_1_out, NQ);
  nor nor_2 (nor_2_out, Q, and_2_out);
  or or_2 (NQ, nor_2_out, or_1_out);
endmodule

module d_trigger (
  input  D,
  input  C,
  input  Enable,
  output Q,
  output NQ
);

  wire not_1_out;

  not not_1 (not_1_out, D);
  rs_trigger_sync rs_trigger_sync_1 (.R(not_1_out), .C(C), .S(D), .Enable(Enable), .Q(Q), .NQ(NQ));
endmodule

module comparator (
  input  [23:0] B,
  input  [23:0] A,
  output res
);

  wire substractor_1_is_neg;

  substractor substractor_1 (.B(B), .A(A), .is_neg(substractor_1_is_neg));  // open: Res
  not not_1 (res, substractor_1_is_neg);
endmodule

module parser (
  input  [15:0] HP_num,
  output [9:0] Mant,
  output [4:0] Exp,
  output Sign
);


  assign Exp = HP_num[14:10];
  assign Mant = HP_num[9:0];
  assign Sign = HP_num[15];
endmodule

module if_is_zero (
  input  [9:0] Mant,
  input  [4:0] Exp,
  input  Sign,
  output Flag,
  output [15:0] Res
);

  wire and_1_out;

  and and_1 (and_1_out, ~Mant[0], ~Mant[1], ~Mant[2], ~Mant[3], ~Mant[4], ~Mant[5], ~Mant[6], ~Mant[7], ~Mant[8], ~Mant[9], ~Exp[0], ~Exp[1], ~Exp[2], ~Exp[3], ~Exp[4]);  // AND_Gate
  and and_2 (Flag, and_1_out, Sign);

  assign Res = {Sign, Exp, Mant};
endmodule

module if_is_nan (
  input  [9:0] Mant,
  input  [4:0] Exp,
  input  Sign,
  output Flag,
  output [15:0] Res
);

  wire and_1_out, or_1_out;

  or or_1 (or_1_out, Mant[0], Mant[1], Mant[2], Mant[3], Mant[4], Mant[5], Mant[6], Mant[7], Mant[8], Mant[9]);
  and and_1 (and_1_out, Exp[0], Exp[1], Exp[2], Exp[3], Exp[4]);
  and and_2 (Flag, or_1_out, and_1_out);

  assign Res = {Sign, Exp, 1'b1, Mant[8:0]};
endmodule

module if_is_pinf (
  input  [9:0] Mant,
  input  [4:0] Exp,
  input  Sign,
  output Flag,
  output [15:0] Res
);

  and and_1 (Flag, ~Mant[0], ~Mant[1], ~Mant[2], ~Mant[3], ~Mant[4], ~Mant[5], ~Mant[6], ~Mant[7], ~Mant[8], ~Mant[9], Exp[0], Exp[1], Exp[2], Exp[3], Exp[4], ~Sign);  // AND_Gate

  assign Res = {Sign, Exp, Mant};
endmodule

module if_is_neg (
  input  [9:0] Mant,
  input  [4:0] Exp,
  input  Sign,
  output Flag,
  output [15:0] Res
);

  wire if_is_nan_1_flag, if_is_zero_1_flag;

  if_is_zero if_is_zero_1 (.Mant(Mant), .Exp(Exp), .Flag(if_is_zero_1_flag));  // open: Sign, Res
  if_is_nan if_is_nan_1 (.Mant(Mant), .Exp(Exp), .Sign(Sign), .Flag(if_is_nan_1_flag));  // open: Res
  and and_1 (Flag, ~if_is_zero_1_flag, ~if_is_nan_1_flag, Sign);  // AND_Gate

  assign Res = 16'hfe00;
endmodule

module if_else_expression (
  input  expression,
  input  [23:0] value_1,
  input  [23:0] value_2,
  output [23:0] res
);

  wire not_1_out;

  not not_1 (not_1_out, expression);
  // Transmission_Gate #(.width(24)) transmission_1: pin names not known; wires that end beside it: value_2, not_1_out, expression, res
  // Transmission_Gate #(.width(24)) transmission_2: pin names not known; wires that end beside it: value_1, expression, not_1_out, res
endmodule

module memory (
  input  [23:0] A,
  input  C,
  input  Enable,
  output [23:0] Res
);

  d_trigger d_trigger_1 (.D(A[0]), .C(C), .Enable(Enable), .Q(Res[0]));  // open: NQ
  d_trigger d_trigger_2 (.D(A[1]), .C(C), .Enable(Enable), .Q(Res[1]));  // open: NQ
  d_trigger d_trigger_3 (.D(A[2]), .C(C), .Enable(Enable), .Q(Res[2]));  // open: NQ
  d_trigger d_trigger_4 (.D(A[3]), .C(C), .Enable(Enable), .Q(Res[3]));  // open: NQ
  d_trigger d_trigger_5 (.D(A[4]), .C(C), .Enable(Enable), .Q(Res[4]));  // open: NQ
  d_trigger d_trigger_6 (.D(A[5]), .C(C), .Enable(Enable), .Q(Res[5]));  // open: NQ
  d_trigger d_trigger_7 (.D(A[6]), .C(C), .Enable(Enable), .Q(Res[6]));  // open: NQ
  d_trigger d_trigger_8 (.D(A[7]), .C(C), .Enable(Enable), .Q(Res[7]));  // open: NQ
  d_trigger d_trigger_9 (.D(A[8]), .C(C), .Enable(Enable), .Q(Res[8]));  // open: NQ
  d_trigger d_trigger_10 (.D(A[9]), .C(C), .Enable(Enable), .Q(Res[9]));  // open: NQ
  d_trigger d_trigger_11 (.D(A[10]), .C(C), .Enable(Enable), .Q(Res[10]));  // open: NQ
  d_trigger d_trigger_12 (.D(A[11]), .C(C), .Enable(Enable), .Q(Res[11]));  // open: NQ
  d_trigger d_trigger_13 (.D(A[12]), .C(C), .Enable(Enable), .Q(Res[12]));  // open: NQ
  d_trigger d_trigger_14 (.D(A[13]), .C(C), .Enable(Enable), .Q(Res[13]));  // open: NQ
  d_trigger d_trigger_15 (.D(A[14]), .C(C), .Enable(Enable), .Q(Res[14]));  // open: NQ
  d_trigger d_trigger_16 (.D(A[15]), .C(C), .Enable(Enable), .Q(Res[15]));  // open: NQ
  d_trigger d_trigger_17 (.D(A[16]), .C(C), .Enable(Enable), .Q(Res[16]));  // open: NQ
  d_trigger d_trigger_18 (.D(A[17]), .C(C), .Enable(Enable), .Q(Res[17]));  // open: NQ
  d_trigger d_trigger_19 (.D(A[18]), .C(C), .Enable(Enable), .Q(Res[18]));  // open: NQ
  d_trigger d_trigger_20 (.D(A[19]), .C(C), .Enable(Enable), .Q(Res[19]));  // open: NQ
  d_trigger d_trigger_21 (.D(A[20]), .C(C), .Enable(Enable), .Q(Res[20]));  // open: NQ
  d_trigger d_trigger_22 (.D(A[21]), .C(C), .Enable(Enable), .Q(Res[21]));  // open: NQ
  d_trigger d_trigger_23 (.D(A[22]), .C(C), .Enable(Enable), .Q(Res[22]));  // open: NQ
  d_trigger d_trigger_24 (.D(A[23]), .C(C), .Enable(Enable), .Q(Res[23]));  // open: NQ
endmodule

module make_correct_exp_mant (
  input  [9:0] Mant,
  input  [4:0] Exp,
  output [23:0] Res_mant,
  output [23:0] Res_exp
);

  wire and_1_out, and_2_out, and_3_out, comparator_1_res, is_num_not_denorm_res, is_one_1_res, is_one_2_res,
       is_one_3_res, is_one_4_res, is_one_5_res, is_one_6_res, is_one_7_res, is_one_8_res, is_one_9_res,
       is_one_10_res;
  wire [23:0] bit_shift_left_1_out_2, bit_shift_left_2_out_2, bit_shift_left_3_out_2, bit_shift_left_4_out_2,
       bit_shift_left_5_out_2, bit_shift_left_6_out_2, bit_shift_left_7_out_2, bit_shift_left_8_out_2,
       bit_shift_left_9_out_2, bit_shift_left_10_out_2, bit_shift_left_11_out_2, bit_shift_left_12_out_2,
       bit_shift_right_1_res, bit_shift_right_2_res, bit_shift_right_3_res, extend_10_to_24_1_res,
       if_denorm_exp_odd_for_exp_res, if_denorm_exp_odd_for_mant_res, if_else_expression_1_res,
       if_else_expression_2_res, if_else_expression_3_res, if_else_expression_4_res,
       if_else_expression_5_res, if_else_expression_6_res, if_else_expression_7_res,
       if_else_expression_8_res, if_else_expression_9_res, if_else_expression_10_res,
       if_else_expression_11_res, if_else_expression_12_res, if_else_expression_13_res,
       if_else_expression_14_res, if_else_expression_15_res, if_else_expression_16_res,
       if_else_expression_17_res, if_else_expression_18_res, if_else_expression_19_res,
       if_else_expression_20_res, if_else_expression_21_res, if_else_expression_22_res,
       if_else_expression_24_res, if_exp_odd_res, substractor_1_res, substractor_2_res, substractor_3_res,
       substractor_4_res, substractor_5_res, summator_1_sum, summator_2_sum, summator_3_sum;

  and and_1 (and_1_out, ~Exp[0], ~Exp[1], ~Exp[2], ~Exp[3], ~Exp[4]);  // AND_Gate
  and and_2 (and_2_out, ~Mant[0], ~Mant[1], ~Mant[2], ~Mant[3], ~Mant[4], ~Mant[5], ~Mant[6], ~Mant[7], ~Mant[8], ~Mant[9]);  // AND_Gate
  and and_3 (and_3_out, and_2_out, and_1_out);
  extend_10_to_24 extend_10_to_24_1 (.A(Mant), .Res(extend_10_to_24_1_res));
  bit_shift_left bit_shift_left_1 (.in_1({14'h1, Mant}), .out_2(bit_shift_left_1_out_2));
  is_one is_one_1 (.A(extend_10_to_24_1_res), .res(is_one_1_res));
  bit_shift_left bit_shift_left_2 (.in_1(extend_10_to_24_1_res), .out_2(bit_shift_left_2_out_2));
  is_one is_one_2 (.A(bit_shift_left_2_out_2), .res(is_one_2_res));
  bit_shift_left bit_shift_left_3 (.in_1(bit_shift_left_2_out_2), .out_2(bit_shift_left_3_out_2));
  is_one is_one_3 (.A(bit_shift_left_3_out_2), .res(is_one_3_res));
  bit_shift_left bit_shift_left_4 (.in_1(bit_shift_left_3_out_2), .out_2(bit_shift_left_4_out_2));
  is_one is_one_4 (.A(bit_shift_left_4_out_2), .res(is_one_4_res));
  bit_shift_left bit_shift_left_5 (.in_1(bit_shift_left_4_out_2), .out_2(bit_shift_left_5_out_2));
  is_one is_one_5 (.A(bit_shift_left_5_out_2), .res(is_one_5_res));
  bit_shift_left bit_shift_left_6 (.in_1(bit_shift_left_5_out_2), .out_2(bit_shift_left_6_out_2));
  is_one is_one_6 (.A(bit_shift_left_6_out_2), .res(is_one_6_res));
  bit_shift_left bit_shift_left_7 (.in_1(bit_shift_left_6_out_2), .out_2(bit_shift_left_7_out_2));
  is_one is_one_7 (.A(bit_shift_left_7_out_2), .res(is_one_7_res));
  bit_shift_left bit_shift_left_8 (.in_1(bit_shift_left_7_out_2), .out_2(bit_shift_left_8_out_2));
  is_one is_one_8 (.A(bit_shift_left_8_out_2), .res(is_one_8_res));
  bit_shift_left bit_shift_left_9 (.in_1(bit_shift_left_8_out_2), .out_2(bit_shift_left_9_out_2));
  is_one is_one_9 (.A(bit_shift_left_9_out_2), .res(is_one_9_res));
  bit_shift_left bit_shift_left_10 (.in_1(bit_shift_left_9_out_2), .out_2(bit_shift_left_10_out_2));
  is_one is_one_10 (.A(bit_shift_left_10_out_2), .res(is_one_10_res));
  bit_shift_left bit_shift_left_11 (.in_1(bit_shift_left_10_out_2), .out_2(bit_shift_left_11_out_2));
  substractor substractor_1 (.B(24'h1), .A({{19{1'b0}}, Exp}), .Res(substractor_1_res));  // open: is_neg
  if_else_expression if_exp_odd (
    .expression(Exp[0]), .value_1({14'h1, Mant}), .value_2(bit_shift_left_1_out_2), .res(if_exp_odd_res));
  if_else_expression if_else_expression_1 (
    .expression(is_one_1_res), .value_1(bit_shift_left_2_out_2), .value_2(if_else_expression_2_res),
    .res(if_else_expression_1_res));
  if_else_expression if_else_expression_2 (
    .expression(is_one_2_res), .value_1(bit_shift_left_3_out_2), .value_2(if_else_expression_3_res),
    .res(if_else_expression_2_res));
  if_else_expression if_else_expression_3 (
    .expression(is_one_3_res), .value_1(bit_shift_left_4_out_2), .value_2(if_else_expression_4_res),
    .res(if_else_expression_3_res));
  if_else_expression if_else_expression_4 (
    .expression(is_one_4_res), .value_1(bit_shift_left_5_out_2), .value_2(if_else_expression_5_res),
    .res(if_else_expression_4_res));
  if_else_expression if_else_expression_5 (
    .expression(is_one_5_res), .value_1(bit_shift_left_6_out_2), .value_2(if_else_expression_6_res),
    .res(if_else_expression_5_res));
  if_else_expression if_else_expression_6 (
    .expression(is_one_6_res), .value_1(bit_shift_left_7_out_2), .value_2(if_else_expression_7_res),
    .res(if_else_expression_6_res));
  if_else_expression if_else_expression_7 (
    .expression(is_one_7_res), .value_1(bit_shift_left_8_out_2), .value_2(if_else_expression_8_res),
    .res(if_else_expression_7_res));
  if_else_expression if_else_expression_8 (
    .expression(is_one_8_res), .value_1(bit_shift_left_9_out_2), .value_2(if_else_expression_9_res),
    .res(if_else_expression_8_res));
  if_else_expression if_else_expression_9 (
    .expression(is_one_9_res), .value_1(bit_shift_left_10_out_2), .value_2(if_else_expression_10_res),
    .res(if_else_expression_9_res));
  if_else_expression if_else_expression_10 (
    .expression(is_one_10_res), .value_1(bit_shift_left_11_out_2), .res(if_else_expression_10_res));  // open: value_2
  if_else_expression if_else_expression_11 (
    .expression(Exp[0]), .value_1({{19{1'b0}}, Exp}), .value_2(substractor_1_res),
    .res(if_else_expression_11_res));
  if_else_expression if_else_expression_12 (
    .expression(is_one_1_res), .value_1(24'h1), .value_2(if_else_expression_13_res),
    .res(if_else_expression_12_res));
  if_else_expression if_else_expression_13 (
    .expression(is_one_2_res), .value_1(24'h2), .value_2(if_else_expression_14_res),
    .res(if_else_expression_13_res));
  if_else_expression if_else_expression_14 (
    .expression(is_one_3_res), .value_1(24'h3), .value_2(if_else_expression_15_res),
    .res(if_else_expression_14_res));
  if_else_expression if_else_expression_15 (
    .expression(is_one_4_res), .value_1(24'h4), .value_2(if_else_expression_16_res),
    .res(if_else_expression_15_res));
  if_else_expression if_else_expression_16 (
    .expression(is_one_5_res), .value_1(24'h5), .value_2(if_else_expression_17_res),
    .res(if_else_expression_16_res));
  if_else_expression if_else_expression_17 (
    .expression(is_one_6_res), .value_1(24'h6), .value_2(if_else_expression_18_res),
    .res(if_else_expression_17_res));
  if_else_expression if_else_expression_18 (
    .expression(is_one_7_res), .value_1(24'h7), .value_2(if_else_expression_19_res),
    .res(if_else_expression_18_res));
  if_else_expression if_else_expression_19 (
    .expression(is_one_8_res), .value_1(24'h8), .value_2(if_else_expression_20_res),
    .res(if_else_expression_19_res));
  if_else_expression if_else_expression_20 (
    .expression(is_one_9_res), .value_1(24'h9), .value_2(if_else_expression_21_res),
    .res(if_else_expression_20_res));
  if_else_expression if_else_expression_21 (
    .expression(is_one_10_res), .value_1(24'ha), .res(if_else_expression_21_res));  // open: value_2
  comparator comparator_1 (.B(if_else_expression_11_res), .A(24'he), .res(comparator_1_res));
  substractor substractor_2 (.B(if_else_expression_11_res), .A(24'hf), .Res(substractor_2_res));  // open: is_neg
  substractor substractor_3 (.B(24'hf), .A(if_else_expression_11_res), .Res(substractor_3_res));  // open: is_neg
  bit_shift_left bit_shift_left_12 (.in_1(if_else_expression_1_res), .out_2(bit_shift_left_12_out_2));
  summator summator_1 (.B(24'h1), .A(summator_2_sum), .Sum(summator_1_sum));
  summator summator_2 (.B(if_else_expression_12_res), .A(24'he), .Sum(summator_2_sum));
  if_else_expression if_else_expression_22 (
    .expression(comparator_1_res), .value_1(substractor_4_res), .value_2(summator_3_sum),
    .res(if_else_expression_22_res));
  bit_shift_right bit_shift_right_1 (.A(substractor_2_res), .Res(bit_shift_right_1_res));
  bit_shift_right bit_shift_right_2 (.A(substractor_3_res), .Res(bit_shift_right_2_res));
  if_else_expression if_denorm_exp_odd_for_mant (
    .expression(if_else_expression_12_res[0]), .value_1(bit_shift_left_12_out_2),
    .value_2(if_else_expression_1_res), .res(if_denorm_exp_odd_for_mant_res));
  if_else_expression if_denorm_exp_odd_for_exp (
    .expression(if_else_expression_12_res[0]), .value_1(summator_1_sum), .value_2(summator_2_sum),
    .res(if_denorm_exp_odd_for_exp_res));
  comparator is_num_not_denorm (.B(24'h1), .A({{19{1'b0}}, Exp}), .res(is_num_not_denorm_res));
  bit_shift_right bit_shift_right_3 (.A(if_denorm_exp_odd_for_exp_res), .Res(bit_shift_right_3_res));
  substractor substractor_4 (.B(bit_shift_right_1_res), .A(24'hf), .Res(substractor_4_res));  // open: is_neg
  summator summator_3 (.B(bit_shift_right_2_res), .A(24'hf), .Sum(summator_3_sum));
  substractor substractor_5 (.B(bit_shift_right_3_res), .A(24'hf), .Res(substractor_5_res));  // open: is_neg
  if_else_expression if_else_expression_23 (
    .expression(is_num_not_denorm_res), .value_1(if_exp_odd_res), .value_2(if_denorm_exp_odd_for_mant_res),
    .res(Res_mant));
  if_else_expression if_else_expression_24 (
    .expression(is_num_not_denorm_res), .value_1(if_else_expression_22_res), .value_2(substractor_5_res),
    .res(if_else_expression_24_res));
  if_else_expression if_else_expression_25 (
    .expression(and_3_out), .value_1({24{1'b0}}), .value_2(if_else_expression_24_res), .res(Res_exp));
endmodule

module jk_trigger_sync (
  input  K,
  input  C,
  input  J,
  input  Enable,
  output Q,
  output NQ
);

  wire and_1_out, and_2_out, not_1_out, rs_trigger_sync_1_nq, rs_trigger_sync_1_q;

  and and_1 (and_1_out, Q, K);
  and and_2 (and_2_out, J, NQ);
  not not_1 (not_1_out, C);
  rs_trigger_sync rs_trigger_sync_1 (
    .R(and_1_out), .C(C), .S(and_2_out), .Enable(Enable), .Q(rs_trigger_sync_1_q), .NQ(rs_trigger_sync_1_nq));
  rs_trigger_sync rs_trigger_sync_2 (
    .R(rs_trigger_sync_1_nq), .C(not_1_out), .S(rs_trigger_sync_1_q), .Enable(Enable), .Q(Q), .NQ(NQ));
endmodule

module counter (
  input  C,
  input  Enable,
  output [15:0] Res
);

  wire jk_trigger_sync_1_nq, jk_trigger_sync_1_q, jk_trigger_sync_2_nq, jk_trigger_sync_2_q,
       jk_trigger_sync_3_nq, jk_trigger_sync_3_q, jk_trigger_sync_4_nq;

  jk_trigger_sync jk_trigger_sync_1 (
    .K(Enable), .C(C), .J(Enable), .Enable(Enable), .Q(jk_trigger_sync_1_q), .NQ(jk_trigger_sync_1_nq));
  jk_trigger_sync jk_trigger_sync_2 (
    .K(Enable), .C(jk_trigger_sync_1_q), .J(Enable), .Enable(Enable), .Q(jk_trigger_sync_2_q),
    .NQ(jk_trigger_sync_2_nq));
  jk_trigger_sync jk_trigger_sync_3 (
    .K(Enable), .C(jk_trigger_sync_2_q), .J(Enable), .Enable(Enable), .Q(jk_trigger_sync_3_q),
    .NQ(jk_trigger_sync_3_nq));
  jk_trigger_sync jk_trigger_sync_4 (
    .K(Enable), .C(jk_trigger_sync_3_q), .J(Enable), .Enable(Enable), .NQ(jk_trigger_sync_4_nq));  // open: Q
  not not_1 (Res[3], jk_trigger_sync_4_nq);
  not not_2 (Res[2], jk_trigger_sync_3_nq);
  not not_3 (Res[1], jk_trigger_sync_2_nq);
  not not_4 (Res[0], jk_trigger_sync_1_nq);

  assign Res[15:4] = {12{1'b0}};
endmodule

module bit_shift_right (
  input  [23:0] A,
  output [23:0] Res
);

  // NoConnect on A[0]

  assign Res = {1'b0, A[23:1]};
endmodule

module sqrt (
  input  CLK,
  input  ENABLE,
  input  [15:0] IO_DATA_IN,
  output IS_NAN,
  output IS_PINF,
  output IS_NINF,
  output RESULT,
  output [15:0] IO_DATA_OUT
);

  wire and_1_out, and_2_out, and_3_out, and_7_out, and_8_out, comparator_2_res, first_tact_passed_q,
       if_is_nan_1_flag, if_is_neg_1_flag, if_is_pinf_1_flag, if_is_zero_1_flag, is_pos_zero,
       is_special_case, more_than_first_tact, more_than_second_tact_res, not_1_out, not_2_out, not_3_out,
       not_4_out, not_5_out, or_1_out, or_2_out, or_3_out, or_4_out, or_5_out, or_6_out, parser_1_sign,
       remember_nan_q, remember_neg_zero_q, remember_ninf_q, remember_pinf_q, remember_result_q,
       twelve_tact_passed;
  wire [4:0] parser_1_exp;
  wire [9:0] final_res, parser_1_mant;
  wire [15:0] counter_num, final_res_extr_cases, if_is_nan_1_res, if_is_neg_1_res, if_is_pinf_1_res,
       if_is_zero_1_res, transistor_1_out, transmission_1_p1;
  wire [23:0] bit_shift_left_1_out_2, bit_shift_left_2_out_2, bit_shift_left_3_out_2, bit_shift_left_4_out_2,
       bit_shift_left_5_out_2, bit_shift_left_6_out_2, exp, extend_2_to_24_1_res, extend_16_to_24_1_res,
       extend_16_to_24_2_res, extend_16_to_24_3_res, extend_16_to_24_4_res, extend_16_to_24_5_res,
       extend_16_to_24_6_res, extend_16_to_24_7_res, if_else_expression_1_res, if_else_expression_2_res,
       if_else_expression_3_res, if_else_expression_4_res, if_else_expression_5_res,
       if_else_expression_6_res, if_else_expression_7_res, if_for_buffer_res, if_rest1_res, if_result1_res,
       if_special_case_res, make_correct_exp_mant_1_res_exp, make_correct_exp_mant_1_res_mant, num1_res,
       num2_res, remember_res_if_extr_case_res, rest1_res, rest2_res, result1_res, result2_res,
       start_print_res_res, substractor_1_res, summator_1_sum, summator_2_sum, summator_3_sum;
  wire [23:10] mant;

  not not_1 (not_1_out, CLK);
  or or_1 (or_1_out, twelve_tact_passed, more_than_second_tact_res);
  extend_16_to_24 extend_16_to_24_1 (.A(counter_num), .Res(extend_16_to_24_1_res));
  d_trigger d_trigger_1 (.D(1'b1), .C(counter_num[1]), .Enable(ENABLE), .Q(more_than_first_tact));  // open: NQ
  if_else_expression start_print_res (
    .expression(or_1_out), .value_1(24'h1), .value_2({24{1'b0}}), .res(start_print_res_res));
  extend_16_to_24 extend_16_to_24_2 (.A(final_res_extr_cases), .Res(extend_16_to_24_2_res));
  extend_16_to_24 extend_16_to_24_3 (.A({1'b0, exp[4:0], final_res}), .Res(extend_16_to_24_3_res));
  parser parser_1 (.HP_num(transistor_1_out), .Mant(parser_1_mant), .Exp(parser_1_exp), .Sign(parser_1_sign));
  counter counter_1 (.C(not_1_out), .Enable(ENABLE), .Res(counter_num));
  and and_1 (and_1_out, ~twelve_tact_passed, ~RESULT, not_1_out);  // AND_Gate
  comparator more_than_second_tact (.B(24'h2), .A(extend_16_to_24_1_res), .res(more_than_second_tact_res));
  not not_2 (not_2_out, start_print_res_res[0]);
  // Transmission_Gate #(.width(16)) transmission_1: pin names not known; wires that end beside it: transmission_1_p1, not_2_out, start_print_res_res[0], IO_DATA_IN
  d_trigger first_tact_passed (.D(1'b1), .C(counter_num[0]), .Enable(ENABLE), .Q(first_tact_passed_q));  // open: NQ
  Transistor #(.width(16)) transistor_1 (.in(IO_DATA_IN), .out(transistor_1_out), .gate(first_tact_passed_q));
  not not_3 (not_3_out, first_tact_passed_q);
  if_else_expression if_special_case (
    .expression(is_special_case), .value_1(extend_16_to_24_2_res), .value_2(extend_16_to_24_3_res),
    .res(if_special_case_res));
  comparator comparator_1 (.B(extend_16_to_24_3_res), .A({24{1'b0}}), .res(is_pos_zero));
  if_is_zero if_is_zero_1 (
    .Mant(parser_1_mant), .Exp(parser_1_exp), .Sign(parser_1_sign), .Flag(if_is_zero_1_flag),
    .Res(if_is_zero_1_res));
  if_is_pinf if_is_pinf_1 (
    .Mant(parser_1_mant), .Exp(parser_1_exp), .Sign(parser_1_sign), .Flag(if_is_pinf_1_flag),
    .Res(if_is_pinf_1_res));
  if_is_nan if_is_nan_1 (
    .Mant(parser_1_mant), .Exp(parser_1_exp), .Sign(parser_1_sign), .Flag(if_is_nan_1_flag),
    .Res(if_is_nan_1_res));
  if_is_neg if_is_neg_1 (
    .Mant(parser_1_mant), .Exp(parser_1_exp), .Sign(parser_1_sign), .Flag(if_is_neg_1_flag),
    .Res(if_is_neg_1_res));
  extend_24_to_16 extend_24_to_16_1 (.Res(if_special_case_res), .A(transmission_1_p1));
  make_correct_exp_mant make_correct_exp_mant_1 (
    .Mant(parser_1_mant), .Exp(parser_1_exp), .Res_mant(make_correct_exp_mant_1_res_mant),
    .Res_exp(make_correct_exp_mant_1_res_exp));
  extend_16_to_24 extend_16_to_24_4 (.A(if_is_zero_1_res), .Res(extend_16_to_24_4_res));
  extend_16_to_24 extend_16_to_24_5 (.A(if_is_pinf_1_res), .Res(extend_16_to_24_5_res));
  extend_16_to_24 extend_16_to_24_6 (.A(if_is_nan_1_res), .Res(extend_16_to_24_6_res));
  extend_16_to_24 extend_16_to_24_7 (.A(if_is_neg_1_res), .Res(extend_16_to_24_7_res));
  and and_2 (and_2_out, ~counter_num[0], ~counter_num[1], counter_num[2], counter_num[3], ~counter_num[4], ~counter_num[5], ~counter_num[6], ~counter_num[7], ~counter_num[8], ~counter_num[9], ~counter_num[10], ~counter_num[11], ~counter_num[12], ~counter_num[13], ~counter_num[14], ~counter_num[15]);  // AND_Gate
  or or_2 (or_2_out, if_is_nan_1_flag, if_is_neg_1_flag);
  or or_3 (or_3_out, if_is_pinf_1_flag, if_is_zero_1_flag, if_is_nan_1_flag, if_is_neg_1_flag);
  or or_4 (or_4_out, not_3_out, and_1_out);
  if_else_expression if_else_expression_1 (
    .expression(if_is_zero_1_flag), .value_1(extend_16_to_24_4_res), .value_2(if_else_expression_2_res),
    .res(if_else_expression_1_res));
  if_else_expression if_else_expression_2 (
    .expression(if_is_pinf_1_flag), .value_1(extend_16_to_24_5_res), .value_2(if_else_expression_3_res),
    .res(if_else_expression_2_res));
  if_else_expression if_else_expression_3 (
    .expression(if_is_nan_1_flag), .value_1(extend_16_to_24_6_res), .value_2(if_else_expression_4_res),
    .res(if_else_expression_3_res));
  if_else_expression if_else_expression_4 (
    .expression(if_is_neg_1_flag), .value_1(extend_16_to_24_7_res), .value_2({24{1'b0}}),
    .res(if_else_expression_4_res));
  if_else_expression if_else_expression_5 (
    .expression(not_3_out), .value_1({24{1'b0}}), .value_2(result2_res), .res(if_else_expression_5_res));
  if_else_expression if_else_expression_6 (
    .expression(not_3_out), .value_1({24{1'b0}}), .value_2(rest2_res), .res(if_else_expression_6_res));
  if_else_expression if_else_expression_7 (
    .expression(not_3_out), .value_1(make_correct_exp_mant_1_res_mant), .value_2(num2_res),
    .res(if_else_expression_7_res));
  d_trigger d_trigger_2 (.D(1'b1), .C(and_2_out), .Enable(ENABLE), .Q(twelve_tact_passed));  // open: NQ
  d_trigger remember_neg_zero (.D(1'b1), .C(if_is_zero_1_flag), .Enable(ENABLE), .Q(remember_neg_zero_q));  // open: NQ
  and and_3 (and_3_out, not_3_out, or_4_out);
  or or_5 (or_5_out, if_is_pinf_1_flag, or_2_out, or_3_out);
  memory num1 (.A(if_else_expression_7_res), .C(or_4_out), .Enable(ENABLE), .Res(num1_res));
  memory rest1 (.A(if_else_expression_6_res), .C(or_4_out), .Enable(ENABLE), .Res(rest1_res));
  memory result1 (.A(if_else_expression_5_res), .C(or_4_out), .Enable(ENABLE), .Res(result1_res));
  d_trigger remember_nan (.D(1'b1), .C(or_2_out), .Enable(ENABLE), .Q(remember_nan_q));  // open: NQ
  d_trigger remember_pinf (.D(1'b1), .C(if_is_pinf_1_flag), .Enable(ENABLE), .Q(remember_pinf_q));  // open: NQ
  d_trigger remember_ninf (.D(1'b1), .C(1'b0), .Enable(ENABLE), .Q(remember_ninf_q));  // open: NQ
  d_trigger remember_result (.D(1'b1), .C(or_3_out), .Enable(ENABLE), .Q(remember_result_q));  // open: NQ
  memory remember_res_if_extr_case (
    .A(if_else_expression_1_res), .C(and_3_out), .Enable(ENABLE), .Res(remember_res_if_extr_case_res));
  memory remember_correct_exp (.A(make_correct_exp_mant_1_res_exp), .C(and_3_out), .Enable(ENABLE), .Res(exp));
  d_trigger d_trigger_3 (.D(1'b1), .C(or_5_out), .Enable(ENABLE), .Q(is_special_case));  // open: NQ
  and and_4 (IS_NAN, remember_nan_q, ~remember_neg_zero_q, more_than_first_tact);  // AND_Gate
  and and_5 (IS_PINF, remember_pinf_q, more_than_first_tact);
  and and_6 (IS_NINF, remember_ninf_q, more_than_first_tact);
  bit_shift_left bit_shift_left_1 (.in_1(num1_res), .out_2(bit_shift_left_1_out_2));
  bit_shift_left bit_shift_left_2 (.in_1(rest1_res), .out_2(bit_shift_left_2_out_2));
  bit_shift_left bit_shift_left_3 (.in_1(result1_res), .out_2(bit_shift_left_3_out_2));
  extend_24_to_16 extend_24_to_16_2 (.Res(remember_res_if_extr_case_res), .A(final_res_extr_cases));
  not not_4 (not_4_out, or_4_out);
  or or_6 (or_6_out, remember_result_q, twelve_tact_passed);
  and and_7 (and_7_out, more_than_first_tact, or_6_out);
  bit_shift_left bit_shift_left_4 (.in_1(bit_shift_left_1_out_2), .out_2(bit_shift_left_4_out_2));
  bit_shift_left bit_shift_left_5 (.in_1(bit_shift_left_2_out_2), .out_2(bit_shift_left_5_out_2));
  bit_shift_left bit_shift_left_6 (.in_1(bit_shift_left_3_out_2), .out_2(bit_shift_left_6_out_2));
  extend_2_to_24 extend_2_to_24_1 (.A(num1_res[11:10]), .Res(extend_2_to_24_1_res));
  and and_8 (and_8_out, more_than_first_tact, is_pos_zero);
  summator summator_1 (.B(bit_shift_left_6_out_2), .A(24'h1), .Sum(summator_1_sum));
  summator summator_2 (.B(24'h1), .A(bit_shift_left_3_out_2), .Sum(summator_2_sum));
  or or_7 (RESULT, and_8_out, and_7_out);
  summator summator_3 (.B(bit_shift_left_5_out_2), .A(extend_2_to_24_1_res), .Sum(summator_3_sum));
  comparator comparator_2 (.B(summator_1_sum), .A(summator_3_sum), .res(comparator_2_res));
  substractor substractor_1 (.B(summator_1_sum), .A(summator_3_sum), .Res(substractor_1_res));  // open: is_neg
  if_else_expression if_result1 (
    .expression(comparator_2_res), .value_1(summator_2_sum), .value_2(bit_shift_left_3_out_2),
    .res(if_result1_res));
  if_else_expression if_rest1 (
    .expression(comparator_2_res), .value_1(substractor_1_res), .value_2(summator_3_sum), .res(if_rest1_res));
  not not_5 (not_5_out, not_4_out);
  memory num2 (.A(bit_shift_left_4_out_2), .C(not_4_out), .Enable(ENABLE), .Res(num2_res));
  memory rest2 (.A(if_rest1_res), .C(not_4_out), .Enable(ENABLE), .Res(rest2_res));
  memory result2 (.A(if_result1_res), .C(not_4_out), .Enable(ENABLE), .Res(result2_res));
  if_else_expression if_for_buffer (
    .expression(not_5_out), .value_1(result2_res), .value_2(result1_res), .res(if_for_buffer_res));
  memory buff (.A(if_for_buffer_res), .C(not_4_out), .Enable(ENABLE), .Res({mant, final_res}));

  assign IO_DATA_OUT = IO_DATA_IN;

  // Other names for the same wires on the sheet: final_res[14:10] = exp[4:0]; mant[9:0] = final_res;
  //   recieve_res = RESULT
endmodule

module is_one (
  input  [23:0] A,
  output res
);


  assign res = A[9];
endmodule

module extend_10_to_24 (
  input  [9:0] A,
  output [23:0] Res
);


  assign Res = {{14{1'b0}}, A};
endmodule

module extend_16_to_24 (
  input  [15:0] A,
  output [23:0] Res
);


  assign Res = {{8{1'b0}}, A};
endmodule

module extend_24_to_16 (
  input  [23:0] Res,
  output [15:0] A
);


  assign A = Res[15:0];
endmodule

module extend_2_to_24 (
  input  [1:0] A,
  output [23:0] Res
);


  assign Res = {{22{1'b0}}, A};
endmodule
